# Fritzing sketch MKR_1010_WiFi_Schematic (saved by Fritzing 0.9.4)
circuit board: 8.46667cm x 5.64444cm
breadboards: 1

parts:
  Mod1 = Arduino MKR Wifi 1010
  Part1 = Adafruit STEMMA Soil Sensor - I2C Capacitive Moisture Sensor [part_number="Adafruit #4026"]
  M1 = LLC200D3SH [package=THT]
  Mod2 = MKR ENV Shield

nets:
  GND: Mod1.GND, Part1.GND, M1.pin3, Mod2.GND
  N1: Mod1.A1, M1.pin2
  +5V: Mod1.+5V, Part1.VIN, M1.pin1, Mod2.5V
  N2: Part1.SDA, Mod2.D11_SDA
  N3: Part1.SCL, Mod2.D12_SCL

notes:
  Water Sensor

custom parts:
  Arduino MKR Wifi 1010: Arduino MKR Wifi 1010, SAMD21 Cortex-M0+ 32bit Low Power ARM MCU,Flash Memory 256 KB, SRAM 32KB, 48mhz clock, Ublok Wifi interface.
  Adafruit STEMMA Soil Sensor - I2C Capacitive Moisture Sensor: Most low cost soil sensors are resistive style, where there's two prongs and the sensor measures the conductivity between the two. These work OK at first, but eventually start to oxidize because of the exposed metal. Even if they're gold plated! The resistivity measurement goes up and up, so you constantly have to re-calibrate your code. Also, resistive measurements don't always work in loose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
  LLC200D3SH: Optomax Digital liquid level switch..
  MKR ENV Shield: arduino MRK ENV Shield Atmospheric pressure sensor, temp and humidity, Lux of ambient light, Ultraviolet sensors in MKR form factor.
