# Fritzing sketch Uno WiFi Fritzing (saved by Fritzing 0.9.4)
breadboards: 1

parts:
  NEOPIXEL1 = Neopixel Strip -- White (30/m) [part_number=1376]
  R1 = Resistor [tolerance=±5% resistance=330 package="2512 [SMD]"]
  JACK1 = 2.1mm DC Barrel Jack
  C2 = Electrolytic Capacitor [capacitance=4.7mF voltage=10V package="300 mil [THT, electrolytic]"]
  M1 = DC Motor
  FET1 = STP16NF06 N-Channel Power MOSFET
  D1 = Diode [package=diode-1n4148]
  JACK2 = 2.1mm DC Barrel Jack

nets:
  N1: NEOPIXEL1.GND, JACK1.switch, C2.-
  N2: NEOPIXEL1.Din, R1.Pin_1
  N3: NEOPIXEL1.+5V, JACK1.center, C2.+
  N4: M1.pin_1, D1.C, JACK2.center
  N5: M1.pin_2, FET1.drain
  N6: FET1.source, JACK2.switch

custom parts:
  Neopixel Strip -- White (30/m): These NeoPixel strips have 30 digitally-addressable pixel LEDs per meter and are very affordable and are only 12.5 mm wide, 10 mm if you remove the strip from the casing.
  2.1mm DC Barrel Jack: 2.1mm DC Barrel Jack with Thru-Hole Connectors (breadboardable)
  STP16NF06 N-Channel Power MOSFET: STP16NF06 N-channel Power MOSFET
